// Digital circuit EEPROM.dig as structural Verilog
module EEPROM (
  input  [3:0] addr,
  input  [3:0] Din,
  input  Rst,
  input  WE,
  input  clk,
  output [3:0] Dout
);

  wire and_1_out, and_2_out, and_3_out, and_4_out, and_5_out, and_6_out, and_7_out, and_8_out, and_9_out,
       and_10_out, and_11_out, and_12_out, and_13_out, and_14_out, and_15_out, and_16_out, and_17_out,
       and_18_out, and_19_out, and_20_out, and_21_out, and_22_out, and_23_out, and_24_out, and_25_out,
       and_26_out, and_27_out, and_28_out, and_29_out, and_30_out, and_31_out, and_32_out, and_33_out,
       and_34_out, and_35_out, and_36_out, and_37_out, and_38_out, and_39_out, and_40_out, and_41_out,
       and_42_out, and_43_out, and_44_out, and_45_out, and_46_out, and_47_out, and_48_out, and_49_out,
       and_50_out, and_51_out, and_52_out, and_53_out, and_54_out, and_55_out, and_56_out, and_57_out,
       and_58_out, and_59_out, and_60_out, and_61_out, and_62_out, and_63_out, and_64_out, and_65_out,
       and_66_out, and_67_out, and_68_out, and_69_out, and_70_out, and_71_out, and_72_out, and_73_out,
       and_74_out, and_75_out, and_76_out, and_77_out, and_78_out, and_79_out, and_80_out, and_81_out,
       decoder_1_out_0, decoder_1_out_1, decoder_1_out_2, decoder_1_out_3, decoder_1_out_4, decoder_1_out_5,
       decoder_1_out_6, decoder_1_out_7, decoder_1_out_8, decoder_1_out_9, decoder_1_out_10,
       decoder_1_out_11, decoder_1_out_12, decoder_1_out_13, decoder_1_out_14, decoder_1_out_15, dff_1_q,
       dff_2_q, dff_3_q, dff_4_q, dff_5_q, dff_6_q, dff_7_q, dff_8_q, dff_9_q, dff_10_q, dff_11_q, dff_12_q,
       dff_13_q, dff_14_q, dff_15_q, dff_16_q, dff_17_q, dff_18_q, dff_19_q, dff_20_q, dff_21_q, dff_22_q,
       dff_23_q, dff_24_q, dff_25_q, dff_26_q, dff_27_q, dff_28_q, dff_29_q, dff_30_q, dff_31_q, dff_32_q,
       dff_33_q, dff_34_q, dff_35_q, dff_36_q, dff_37_q, dff_38_q, dff_39_q, dff_40_q, dff_41_q, dff_42_q,
       dff_43_q, dff_44_q, dff_45_q, dff_46_q, dff_47_q, dff_48_q, dff_49_q, dff_50_q, dff_51_q, dff_52_q,
       dff_53_q, dff_54_q, dff_55_q, dff_56_q, dff_57_q, dff_58_q, dff_59_q, dff_60_q, dff_61_q, dff_62_q,
       dff_63_q, dff_64_q, or_1_out, or_2_out, or_3_out, or_4_out, or_5_out, or_6_out, or_7_out, or_8_out,
       or_9_out, or_10_out, or_11_out, or_12_out, or_13_out, or_14_out, or_15_out, or_16_out;
  wire [3:0] multiplexer_1_out;

  and and_1 (and_1_out, clk, WE);
  Decoder #(.Selector_Bits(4)) decoder_1 (
    .sel(addr), .out_0(decoder_1_out_0), .out_1(decoder_1_out_1), .out_2(decoder_1_out_2),
    .out_3(decoder_1_out_3), .out_4(decoder_1_out_4), .out_5(decoder_1_out_5), .out_6(decoder_1_out_6),
    .out_7(decoder_1_out_7), .out_8(decoder_1_out_8), .out_9(decoder_1_out_9), .out_10(decoder_1_out_10),
    .out_11(decoder_1_out_11), .out_12(decoder_1_out_12), .out_13(decoder_1_out_13),
    .out_14(decoder_1_out_14), .out_15(decoder_1_out_15));
  or or_1 (or_1_out, decoder_1_out_0, Rst);
  or or_2 (or_2_out, decoder_1_out_1, Rst);
  or or_3 (or_3_out, decoder_1_out_2, Rst);
  or or_4 (or_4_out, decoder_1_out_3, Rst);
  or or_5 (or_5_out, decoder_1_out_4, Rst);
  or or_6 (or_6_out, decoder_1_out_5, Rst);
  or or_7 (or_7_out, decoder_1_out_6, Rst);
  or or_8 (or_8_out, decoder_1_out_7, Rst);
  or or_9 (or_9_out, decoder_1_out_8, Rst);
  or or_10 (or_10_out, decoder_1_out_9, Rst);
  or or_11 (or_11_out, decoder_1_out_10, Rst);
  or or_12 (or_12_out, decoder_1_out_11, Rst);
  or or_13 (or_13_out, decoder_1_out_12, Rst);
  or or_14 (or_14_out, decoder_1_out_13, Rst);
  or or_15 (or_15_out, decoder_1_out_14, Rst);
  or or_16 (or_16_out, decoder_1_out_15, Rst);
  and and_2 (and_2_out, and_1_out, or_1_out);
  and and_3 (and_3_out, and_1_out, or_2_out);
  and and_4 (and_4_out, and_1_out, or_3_out);
  and and_5 (and_5_out, and_1_out, or_4_out);
  and and_6 (and_6_out, and_1_out, or_5_out);
  and and_7 (and_7_out, and_1_out, or_6_out);
  and and_8 (and_8_out, and_1_out, or_7_out);
  and and_9 (and_9_out, and_1_out, or_8_out);
  and and_10 (and_10_out, and_1_out, or_9_out);
  and and_11 (and_11_out, and_1_out, or_10_out);
  and and_12 (and_12_out, and_1_out, or_11_out);
  and and_13 (and_13_out, and_1_out, or_12_out);
  and and_14 (and_14_out, and_1_out, or_13_out);
  and and_15 (and_15_out, and_1_out, or_14_out);
  and and_16 (and_16_out, and_1_out, or_15_out);
  and and_17 (and_17_out, and_1_out, or_16_out);
  Dff dff_1 (.D(multiplexer_1_out[3]), .clk(and_2_out), .Q(dff_1_q));
  Dff dff_2 (.D(multiplexer_1_out[3]), .clk(and_3_out), .Q(dff_2_q));
  Dff dff_3 (.D(multiplexer_1_out[3]), .clk(and_4_out), .Q(dff_3_q));
  Dff dff_4 (.D(multiplexer_1_out[3]), .clk(and_5_out), .Q(dff_4_q));
  Dff dff_5 (.D(multiplexer_1_out[3]), .clk(and_6_out), .Q(dff_5_q));
  Dff dff_6 (.D(multiplexer_1_out[3]), .clk(and_7_out), .Q(dff_6_q));
  Dff dff_7 (.D(multiplexer_1_out[3]), .clk(and_8_out), .Q(dff_7_q));
  Dff dff_8 (.D(multiplexer_1_out[3]), .clk(and_9_out), .Q(dff_8_q));
  Dff dff_9 (.D(multiplexer_1_out[3]), .clk(and_10_out), .Q(dff_9_q));
  Dff dff_10 (.D(multiplexer_1_out[3]), .clk(and_11_out), .Q(dff_10_q));
  Dff dff_11 (.D(multiplexer_1_out[3]), .clk(and_12_out), .Q(dff_11_q));
  Dff dff_12 (.D(multiplexer_1_out[3]), .clk(and_13_out), .Q(dff_12_q));
  Dff dff_13 (.D(multiplexer_1_out[3]), .clk(and_14_out), .Q(dff_13_q));
  Dff dff_14 (.D(multiplexer_1_out[3]), .clk(and_15_out), .Q(dff_14_q));
  Dff dff_15 (.D(multiplexer_1_out[3]), .clk(and_16_out), .Q(dff_15_q));
  Dff dff_16 (.D(multiplexer_1_out[3]), .clk(and_17_out), .Q(dff_16_q));
  and and_18 (and_18_out, or_16_out, dff_16_q);
  and and_19 (and_19_out, or_14_out, dff_14_q);
  and and_20 (and_20_out, or_15_out, dff_15_q);
  and and_21 (and_21_out, or_12_out, dff_12_q);
  and and_22 (and_22_out, or_13_out, dff_13_q);
  and and_23 (and_23_out, or_10_out, dff_10_q);
  and and_24 (and_24_out, or_11_out, dff_11_q);
  and and_25 (and_25_out, or_8_out, dff_8_q);
  and and_26 (and_26_out, or_9_out, dff_9_q);
  or or_17 (Dout[3], and_33_out, and_31_out, and_32_out, and_29_out, and_30_out, and_27_out, and_28_out, and_25_out, and_26_out, and_23_out, and_24_out, and_21_out, and_22_out, and_19_out, and_20_out, and_18_out);
  and and_27 (and_27_out, or_6_out, dff_6_q);
  and and_28 (and_28_out, or_7_out, dff_7_q);
  and and_29 (and_29_out, or_4_out, dff_4_q);
  and and_30 (and_30_out, or_5_out, dff_5_q);
  and and_31 (and_31_out, or_2_out, dff_2_q);
  and and_32 (and_32_out, or_3_out, dff_3_q);
  and and_33 (and_33_out, or_1_out, dff_1_q);
  Multiplexer #(.Bits(4)) multiplexer_1 (.sel(Rst), .in_0(Din), .in_1(4'b0000), .out(multiplexer_1_out));
  Dff dff_17 (.D(multiplexer_1_out[2]), .clk(and_2_out), .Q(dff_17_q));
  Dff dff_18 (.D(multiplexer_1_out[2]), .clk(and_3_out), .Q(dff_18_q));
  Dff dff_19 (.D(multiplexer_1_out[2]), .clk(and_4_out), .Q(dff_19_q));
  Dff dff_20 (.D(multiplexer_1_out[2]), .clk(and_5_out), .Q(dff_20_q));
  Dff dff_21 (.D(multiplexer_1_out[2]), .clk(and_6_out), .Q(dff_21_q));
  Dff dff_22 (.D(multiplexer_1_out[2]), .clk(and_7_out), .Q(dff_22_q));
  Dff dff_23 (.D(multiplexer_1_out[2]), .clk(and_8_out), .Q(dff_23_q));
  Dff dff_24 (.D(multiplexer_1_out[2]), .clk(and_9_out), .Q(dff_24_q));
  Dff dff_25 (.D(multiplexer_1_out[2]), .clk(and_10_out), .Q(dff_25_q));
  Dff dff_26 (.D(multiplexer_1_out[2]), .clk(and_11_out), .Q(dff_26_q));
  Dff dff_27 (.D(multiplexer_1_out[2]), .clk(and_12_out), .Q(dff_27_q));
  Dff dff_28 (.D(multiplexer_1_out[2]), .clk(and_13_out), .Q(dff_28_q));
  Dff dff_29 (.D(multiplexer_1_out[2]), .clk(and_14_out), .Q(dff_29_q));
  Dff dff_30 (.D(multiplexer_1_out[2]), .clk(and_15_out), .Q(dff_30_q));
  Dff dff_31 (.D(multiplexer_1_out[2]), .clk(and_16_out), .Q(dff_31_q));
  Dff dff_32 (.D(multiplexer_1_out[2]), .clk(and_17_out), .Q(dff_32_q));
  and and_34 (and_34_out, or_15_out, dff_31_q);
  and and_35 (and_35_out, or_16_out, dff_32_q);
  and and_36 (and_36_out, or_13_out, dff_29_q);
  and and_37 (and_37_out, or_14_out, dff_30_q);
  and and_38 (and_38_out, or_11_out, dff_27_q);
  and and_39 (and_39_out, or_12_out, dff_28_q);
  and and_40 (and_40_out, or_9_out, dff_25_q);
  and and_41 (and_41_out, or_10_out, dff_26_q);
  or or_18 (Dout[2], and_48_out, and_49_out, and_46_out, and_47_out, and_44_out, and_45_out, and_42_out, and_43_out, and_40_out, and_41_out, and_38_out, and_39_out, and_36_out, and_37_out, and_34_out, and_35_out);
  and and_42 (and_42_out, or_7_out, dff_23_q);
  and and_43 (and_43_out, or_8_out, dff_24_q);
  and and_44 (and_44_out, or_5_out, dff_21_q);
  and and_45 (and_45_out, or_6_out, dff_22_q);
  and and_46 (and_46_out, or_3_out, dff_19_q);
  and and_47 (and_47_out, or_4_out, dff_20_q);
  and and_48 (and_48_out, or_1_out, dff_17_q);
  and and_49 (and_49_out, or_2_out, dff_18_q);
  Dff dff_33 (.D(multiplexer_1_out[1]), .clk(and_2_out), .Q(dff_33_q));
  Dff dff_34 (.D(multiplexer_1_out[1]), .clk(and_3_out), .Q(dff_34_q));
  Dff dff_35 (.D(multiplexer_1_out[1]), .clk(and_4_out), .Q(dff_35_q));
  Dff dff_36 (.D(multiplexer_1_out[1]), .clk(and_5_out), .Q(dff_36_q));
  Dff dff_37 (.D(multiplexer_1_out[1]), .clk(and_6_out), .Q(dff_37_q));
  Dff dff_38 (.D(multiplexer_1_out[1]), .clk(and_7_out), .Q(dff_38_q));
  Dff dff_39 (.D(multiplexer_1_out[1]), .clk(and_8_out), .Q(dff_39_q));
  Dff dff_40 (.D(multiplexer_1_out[1]), .clk(and_9_out), .Q(dff_40_q));
  Dff dff_41 (.D(multiplexer_1_out[1]), .clk(and_10_out), .Q(dff_41_q));
  Dff dff_42 (.D(multiplexer_1_out[1]), .clk(and_11_out), .Q(dff_42_q));
  Dff dff_43 (.D(multiplexer_1_out[1]), .clk(and_12_out), .Q(dff_43_q));
  Dff dff_44 (.D(multiplexer_1_out[1]), .clk(and_13_out), .Q(dff_44_q));
  Dff dff_45 (.D(multiplexer_1_out[1]), .clk(and_14_out), .Q(dff_45_q));
  Dff dff_46 (.D(multiplexer_1_out[1]), .clk(and_15_out), .Q(dff_46_q));
  Dff dff_47 (.D(multiplexer_1_out[1]), .clk(and_16_out), .Q(dff_47_q));
  Dff dff_48 (.D(multiplexer_1_out[1]), .clk(and_17_out), .Q(dff_48_q));
  and and_50 (and_50_out, or_16_out, dff_48_q);
  and and_51 (and_51_out, or_14_out, dff_46_q);
  and and_52 (and_52_out, or_15_out, dff_47_q);
  and and_53 (and_53_out, or_12_out, dff_44_q);
  and and_54 (and_54_out, or_13_out, dff_45_q);
  and and_55 (and_55_out, or_10_out, dff_42_q);
  and and_56 (and_56_out, or_11_out, dff_43_q);
  and and_57 (and_57_out, or_8_out, dff_40_q);
  and and_58 (and_58_out, or_9_out, dff_41_q);
  or or_19 (Dout[1], and_65_out, and_63_out, and_64_out, and_61_out, and_62_out, and_59_out, and_60_out, and_57_out, and_58_out, and_55_out, and_56_out, and_53_out, and_54_out, and_51_out, and_52_out, and_50_out);
  and and_59 (and_59_out, or_6_out, dff_38_q);
  and and_60 (and_60_out, or_7_out, dff_39_q);
  and and_61 (and_61_out, or_4_out, dff_36_q);
  and and_62 (and_62_out, or_5_out, dff_37_q);
  and and_63 (and_63_out, or_2_out, dff_34_q);
  and and_64 (and_64_out, or_3_out, dff_35_q);
  and and_65 (and_65_out, or_1_out, dff_33_q);
  Dff dff_49 (.D(multiplexer_1_out[0]), .clk(and_2_out), .Q(dff_49_q));
  Dff dff_50 (.D(multiplexer_1_out[0]), .clk(and_3_out), .Q(dff_50_q));
  Dff dff_51 (.D(multiplexer_1_out[0]), .clk(and_4_out), .Q(dff_51_q));
  Dff dff_52 (.D(multiplexer_1_out[0]), .clk(and_5_out), .Q(dff_52_q));
  Dff dff_53 (.D(multiplexer_1_out[0]), .clk(and_6_out), .Q(dff_53_q));
  Dff dff_54 (.D(multiplexer_1_out[0]), .clk(and_7_out), .Q(dff_54_q));
  Dff dff_55 (.D(multiplexer_1_out[0]), .clk(and_8_out), .Q(dff_55_q));
  Dff dff_56 (.D(multiplexer_1_out[0]), .clk(and_9_out), .Q(dff_56_q));
  Dff dff_57 (.D(multiplexer_1_out[0]), .clk(and_10_out), .Q(dff_57_q));
  Dff dff_58 (.D(multiplexer_1_out[0]), .clk(and_11_out), .Q(dff_58_q));
  Dff dff_59 (.D(multiplexer_1_out[0]), .clk(and_12_out), .Q(dff_59_q));
  Dff dff_60 (.D(multiplexer_1_out[0]), .clk(and_13_out), .Q(dff_60_q));
  Dff dff_61 (.D(multiplexer_1_out[0]), .clk(and_14_out), .Q(dff_61_q));
  Dff dff_62 (.D(multiplexer_1_out[0]), .clk(and_15_out), .Q(dff_62_q));
  Dff dff_63 (.D(multiplexer_1_out[0]), .clk(and_16_out), .Q(dff_63_q));
  Dff dff_64 (.D(multiplexer_1_out[0]), .clk(and_17_out), .Q(dff_64_q));
  and and_66 (and_66_out, or_16_out, dff_64_q);
  and and_67 (and_67_out, or_14_out, dff_62_q);
  and and_68 (and_68_out, or_15_out, dff_63_q);
  and and_69 (and_69_out, or_12_out, dff_60_q);
  and and_70 (and_70_out, or_13_out, dff_61_q);
  and and_71 (and_71_out, or_10_out, dff_58_q);
  and and_72 (and_72_out, or_11_out, dff_59_q);
  and and_73 (and_73_out, or_8_out, dff_56_q);
  and and_74 (and_74_out, or_9_out, dff_57_q);
  or or_20 (Dout[0], and_81_out, and_79_out, and_80_out, and_77_out, and_78_out, and_75_out, and_76_out, and_73_out, and_74_out, and_71_out, and_72_out, and_69_out, and_70_out, and_67_out, and_68_out, and_66_out);
  and and_75 (and_75_out, or_6_out, dff_54_q);
  and and_76 (and_76_out, or_7_out, dff_55_q);
  and and_77 (and_77_out, or_4_out, dff_52_q);
  and and_78 (and_78_out, or_5_out, dff_53_q);
  and and_79 (and_79_out, or_2_out, dff_50_q);
  and and_80 (and_80_out, or_3_out, dff_51_q);
  and and_81 (and_81_out, or_1_out, dff_49_q);
endmodule
