// Digital circuit RhCount.dig as structural Verilog
module RhCount (
  input  clk,
  input  C,
  input  Rst,
  output [3:0] Rh
);

  Counter #(.Bits(4)) counter_1 (.en(C), .C(clk), .clr(Rst), .out(Rh));  // open: ovf

  // Notes on the sheet:
  //   Rh: Higher four bits of the result
endmodule
