// Digital circuit adder2bitfull.dig as structural Verilog
module adder2bitfull (
  input  Ah,
  input  Al,
  input  Bh,
  input  Bl,
  output C,
  output Q1,
  output Q0
);

  wire and_1_out, and_2_out, nand_1_out, nand_2_out, nand_3_out, nor_1_out, nor_3_out;

  nand nand_1 (nand_1_out, Ah, Bh);
  and and_1 (and_1_out, ~Ah, ~Bh);  // And
  nand nand_2 (nand_2_out, Al, Bl);
  and and_2 (and_2_out, ~Al, ~Bl);  // And
  nor nor_1 (nor_1_out, ~nand_1_out, and_1_out);  // NOr
  nor nor_2 (Q0, ~nand_2_out, and_2_out);  // NOr
  nand nand_3 (nand_3_out, nor_1_out, ~nand_2_out);  // NAnd
  nor nor_3 (nor_3_out, nor_1_out, ~nand_2_out);  // NOr
  or or_1 (C, ~nand_1_out, ~nand_3_out);  // Or
  nor nor_4 (Q1, ~nand_3_out, nor_3_out);  // NOr
endmodule
