// Digital circuit adder4bithalf.dig as structural Verilog
module adder4bithalf (
  input  [3:0] A,
  input  [3:0] B,
  output C,
  output [3:0] Rl
);

  wire adder2bitfull_1_c, adder2bitfull_1_q0, adder2bitfull_1_q1, adder2bitfull_2_c, and_1_out, and_2_out,
       and_3_out, and_4_out, and_5_out, and_6_out;

  adder2bitfull adder2bitfull_1 (
    .Ah(A[3]), .Al(A[2]), .Bh(B[3]), .Bl(B[2]), .C(adder2bitfull_1_c), .Q1(adder2bitfull_1_q1),
    .Q0(adder2bitfull_1_q0));
  adder2bitfull adder2bitfull_2 (
    .Ah(A[1]), .Al(A[0]), .Bh(B[1]), .Bl(B[0]), .C(adder2bitfull_2_c), .Q1(Rl[1]), .Q0(Rl[0]));
  and and_1 (and_1_out, adder2bitfull_1_q0, adder2bitfull_2_c);
  and and_2 (and_2_out, ~adder2bitfull_1_q0, ~adder2bitfull_2_c);  // And
  and and_3 (and_3_out, adder2bitfull_1_q1, and_1_out);
  and and_4 (and_4_out, ~adder2bitfull_1_q1, ~and_1_out);  // And
  nor nor_1 (Rl[2], and_1_out, and_2_out);
  and and_5 (and_5_out, adder2bitfull_1_c, and_3_out);
  and and_6 (and_6_out, ~adder2bitfull_1_c, ~and_3_out);  // And
  nor nor_2 (Rl[3], and_3_out, and_4_out);
  nor nor_3 (C, and_5_out, and_6_out);

  // Notes on the sheet:
  //   C: carry (R4)
  //   Rl: Lower four bits of the result
endmodule
