// Digital circuit buffer4bit.dig as structural Verilog
module buffer4bit (
  input  Rst,
  input  clk,
  input  [3:0] Din,
  output [3:0] Dout
);

  wire [3:0] multiplexer_1_out;

  Multiplexer #(.Bits(4)) multiplexer_1 (.sel(Rst), .in_0(Din), .in_1(4'b0000), .out(multiplexer_1_out));
  Dff dff_1 (.D(multiplexer_1_out[0]), .clk(clk), .Q(Dout[0]));
  Dff dff_2 (.D(multiplexer_1_out[1]), .clk(clk), .Q(Dout[1]));
  Dff dff_3 (.D(multiplexer_1_out[2]), .clk(clk), .Q(Dout[2]));
  Dff dff_4 (.D(multiplexer_1_out[3]), .clk(clk), .Q(Dout[3]));
endmodule
