// Digital circuit buffer8bit.dig as structural Verilog
module buffer8bit (
  input  [3:0] Rh,
  input  [3:0] Rl,
  input  Rst,
  input  clk,
  output [7:0] Result
);

  wire [7:0] dff_1_q;

  Dff dff_1 (.D(Rh[3]), .clk(clk), .Q(dff_1_q[7]));
  Dff dff_2 (.D(Rh[2]), .clk(clk), .Q(dff_1_q[6]));
  Dff dff_3 (.D(Rh[1]), .clk(clk), .Q(dff_1_q[5]));
  Dff dff_4 (.D(Rh[0]), .clk(clk), .Q(dff_1_q[4]));
  Dff dff_5 (.D(Rl[3]), .clk(clk), .Q(dff_1_q[3]));
  Dff dff_6 (.D(Rl[2]), .clk(clk), .Q(dff_1_q[2]));
  Dff dff_7 (.D(Rl[1]), .clk(clk), .Q(dff_1_q[1]));
  Dff dff_8 (.D(Rl[0]), .clk(clk), .Q(dff_1_q[0]));
  Multiplexer #(.Bits(8)) multiplexer_1 (.sel(Rst), .in_0({8{1'b0}}), .in_1(dff_1_q), .out(Result));
endmodule
