// Digital circuit isMax.dig as structural Verilog
module isMax (
  input  [3:0] N,
  input  [3:0] Addr,
  output rst
);

  wire xnor_1_out, xnor_2_out, xnor_3_out, xnor_4_out;

  xnor xnor_1 (xnor_1_out, N[0], Addr[0]);
  xnor xnor_2 (xnor_2_out, N[1], Addr[1]);
  xnor xnor_3 (xnor_3_out, N[2], Addr[2]);
  xnor xnor_4 (xnor_4_out, N[3], Addr[3]);
  and and_1 (rst, xnor_1_out, xnor_2_out, xnor_3_out, xnor_4_out);
endmodule
