// Digital circuit main.dig as structural Verilog
module main (
  input  [3:0] N,
  input  [3:0] data,
  input  write,
  input  [3:0] addr,
  input  forceRst,
  input  clock,
  output [7:0] Result
);

  wire adder4bithalf_1_c, clk, ismax_1_rst, rst, str;
  wire [3:0] adder4bithalf_1_rl, buffer4bit_1_dout, counter_1_out, eeprom_1_dout, multiplexer_1_out,
       rhcount_1_rh;

  Demultiplexer demultiplexer_1 (.sel(write), .in(clock), .out_0(clk), .out_1(str));
  Counter #(.Bits(4)) counter_1 (.en(1'b1), .C(clk), .clr(rst), .out(counter_1_out));  // open: ovf
  Multiplexer #(.Bits(4)) multiplexer_1 (.sel(write), .in_0(counter_1_out), .in_1(addr), .out(multiplexer_1_out));
  isMax ismax_1 (.N(N), .Addr(counter_1_out), .rst(ismax_1_rst));
  EEPROM eeprom_1 (.addr(multiplexer_1_out), .Din(data), .Rst(rst), .WE(write), .clk(str), .Dout(eeprom_1_dout));
  or or_1 (rst, forceRst, ismax_1_rst);
  adder4bithalf adder4bithalf_1 (
    .A(eeprom_1_dout), .B(buffer4bit_1_dout), .C(adder4bithalf_1_c), .Rl(adder4bithalf_1_rl));
  buffer4bit buffer4bit_1 (.Rst(rst), .clk(clk), .Din(adder4bithalf_1_rl), .Dout(buffer4bit_1_dout));
  RhCount rhcount_1 (.clk(clk), .C(adder4bithalf_1_c), .Rst(rst), .Rh(rhcount_1_rh));
  buffer8bit buffer8bit_1 (.Rh(rhcount_1_rh), .Rl(adder4bithalf_1_rl), .Rst(rst), .clk(clk), .Result(Result));

  // Notes on the sheet:
  //   N: default 3
endmodule
